# Fritzing sketch nilblinky2 (saved by Fritzing 0.9.3b)
breadboards: 1

parts:
  Bauteil1 = STM32-Nucleo32
  LED1 = LED - 5mm [color="Yellow (585nm)" package="5 mm [THT]"]
  S1 = Pushbutton [package="[THT]"]
  C1 = Ceramic Capacitor [capacitance=208nF package="100 mil [THT, multilayer]"]
  R1 = Resistor [tolerance=±5% resistance=100k package=THT]
  R2 = Resistor [tolerance=±5% resistance=10k package=THT]

nets:
  N1: Bauteil1.GND, LED1.cathode, S1.Pin_1, S1.Pin_2, C1.0
  N2: Bauteil1.D3, LED1.anode
  N3: Bauteil1.D8, C1.1, R2.Pin_0
  N4: Bauteil1.3V3, R1.Pin_0
  N5: S1.Pin_3, S1.Pin_4, R1.Pin_1, R2.Pin_1
